# Fritzing sketch main (saved by Fritzing 0.9.0b)
circuit board: 8.46667cm x 5.64444cm
breadboards: 1

parts:
  Composant1 = Arduino Nano (Rev3.0) (ICSP)
  DHT1 = DHT11 Humitidy and Temperature Sensor
  DS1 = DS18B20 1-Wire Temperature Sensor Probe Cable
  Power_plug1 = Power plug
  J3 = screw terminal, 3 pins
  R1 = Resistor [tolerance=±5% resistance=220 package=THT]
  connexion_relais = female pin header, 4 pins [form="♀ (female)"]
  connexion_sim800 = female pin header, 7 pins [form="♀ (female)"]

nets:
  GND: Composant1.GND, DHT1.GND, DS1.GND, Power_plug1.GND, J3.pin2, connexion_relais.pin1, connexion_sim800.pin6
  N1: Composant1.D4, DHT1.DATA
  N2: Composant1.D7, DS1.DQ, J3.pin1, R1.Pin_0
  N3: Composant1.D8, connexion_sim800.pin4
  N4: Composant1.D9, connexion_sim800.pin3
  N5: Composant1.D10, connexion_sim800.pin1
  N6: Composant1.D11/MOSI, connexion_relais.pin2
  N7: Composant1.D12/MISO, connexion_relais.pin3
  VDD: Composant1.5V, DHT1.VDD, DS1.VDD, Power_plug1.VCC, J3.pin3, R1.Pin_1, connexion_relais.pin4, connexion_sim800.pin7

custom parts:
  DHT11 Humitidy and Temperature Sensor: DHT11 Humidity and Temperature Sensor
