# Fritzing sketch boiler (saved by Fritzing 0.9.0b)
circuit board: 7cm x 5cm
breadboards: 1

parts:
  R1 = Resistor [tolerance=±5% resistance=4.7k package=THT]
  Composant1 = Arduino Nano (Rev3.0)
  Smoke = female pin header, 4 pins [form="♀ (female)"]
  DS1 = DS18B20 1-Wire Temperature Sensor Probe Cable  # not connected
  DS2 = DS18B20 1-Wire Temperature Sensor Probe Cable  # not connected
  DS3 = DS18B20 1-Wire Temperature Sensor Probe Cable  # not connected
  J6 = screw terminal, 3 pins
  Light = screw terminal, 3 pins
  Pressure = screw terminal, 4 pins
  Composant2 = NRF24L01

nets:
  N1: R1.Pin_0, Composant1.5V, Smoke.pin1, J6.pin3, Pressure.pin2
  N2: R1.Pin_1, Composant1.D3, J6.pin1
  GND: Composant1.GND, Smoke.pin2, J6.pin2, Pressure.pin1, Composant2.GND
  N3: Composant1.D9, Composant2.CE
  N4: Composant1.D10, Composant2.CSN
  N5: Composant1.D11/MOSI, Composant2.MOSI
  N6: Composant1.D12/MISO, Composant2.MISO
  N7: Composant1.A5, Pressure.pin3
  N8: Composant1.A4, Pressure.pin4
  N9: Composant1.A1, Light.pin2
  N10: Composant1.A0, Smoke.pin4
  3V3: Composant1.3V3, Composant2.VCC
  N11: Composant1.D13/SCK, Composant2.SCK
