# Fritzing sketch hotwater (saved by Fritzing 0.9.3b)
circuit board: 7cm x 5cm
breadboards: 1

parts:
  R1 = Resistor [tolerance=±5% resistance=4.7k package=THT]
  Composant1 = Arduino Nano (Rev3.0)
  DS1 = DS18B20 1-Wire Temperature Sensor Probe Cable  # not connected
  DS2 = DS18B20 1-Wire Temperature Sensor Probe Cable  # not connected
  DS3 = DS18B20 1-Wire Temperature Sensor Probe Cable  # not connected
  J6 = screw terminal, 3 pins
  Composant2 = NRF24L01
  U1 = 2-Channel 5v Relay Shield [package=relay-2ch5v10a]
  U2 = 2-Channel 5v Relay Shield [package=relay-2ch5v10a]
  J9 = female pin header, 4 pins [form="♀ (female)"]
  J10 = female pin header, 4 pins [form="♀ (female)"]
  J11 = Screw terminal - 2 pins [package=THT]

nets:
  VCC: R1.Pin_0, Composant1.5V, U1.VCC, U2.VCC, J9.pin4, J10.pin4, J11.pin1
  N1: R1.Pin_1, Composant1.D7, J6.pin1
  GND: Composant1.GND, J6.pin2, Composant2.GND, U1.GND, U2.GND, J9.pin1, J10.pin1, J11.pin2
  N2: Composant1.D2, U1.IN2, J9.pin3
  N3: Composant1.D3, U1.IN1, J9.pin2
  N4: Composant1.D4, U2.IN2, J10.pin3
  N5: Composant1.D5, U2.IN1, J10.pin2
  N6: Composant1.D9, Composant2.CE
  N7: Composant1.D10, Composant2.CSN
  N8: Composant1.D11/MOSI, Composant2.MOSI
  N9: Composant1.D12/MISO, Composant2.MISO
  3V3: Composant1.3V3, Composant2.VCC
  N10: Composant1.D13/SCK, Composant2.SCK

custom parts:
  2-Channel 5v Relay Shield: 2 Channel 5v Relay Shield w. 2x SPD-06VDC-SD-C
